# Fritzing sketch Ligações Controle de Brassagem automatizado (saved by Fritzing 0.9.4)
breadboards: 1

parts:
  Raspberry_Pi_1 = Raspberry Pi 3 [part_number=RPI-3-V1.2]
  R1 = Resistor [tolerance=±5% resistance=4.7k package=THT]
  R2 = Resistor [tolerance=±5% resistance=4.7k package=THT]
  DS1 = DS18B20 1-Wire Temperature Sensor [part_number=DS18B20]
  DS2 = DS18B20 1-Wire Temperature Sensor [part_number=DS18B20]
  KY-1 = Keyes Relay [package=THT]
  KY-2 = Keyes Relay [package=THT]
  KY-3 = Keyes Relay [package=THT]
  KY-4 = Keyes Relay [package=THT]
  KY-5 = Keyes Relay [package=THT]
  M1 = RioRand LM2596

nets:
  3V3: Raspberry_Pi_1.3v3, Raspberry_Pi_1.3V3, R1.Pin_0, R2.Pin_0, DS1.VDD, DS2.VDD
  N1: Raspberry_Pi_1.GIPO4, R1.Pin_1, R2.Pin_1, DS1.DQ, DS2.DQ
  N2: Raspberry_Pi_1.GIPO5, KY-5.signal
  N3: Raspberry_Pi_1.GIPO6, KY-4.signal
  N4: Raspberry_Pi_1.GIPO13, KY-3.signal
  N5: Raspberry_Pi_1.GIPO26, KY-2.signal
  N6: Raspberry_Pi_1.GIPO16, KY-1.signal
  GND: Raspberry_Pi_1.GND, DS1.GND, DS2.GND, M1.Pin_4
  N7: Raspberry_Pi_1.5V, M1.Pin_3

notes:
  Fonte 12V
  Sensores de temperatura DS128B20
  Relés para acionamento de bomba, motores e resistências

custom parts:
  Keyes Relay: The Keyes 5V relay module is suitable for SCM development, home appliance control. It uses a 5V~12V TIL control signal which can control DC / AC signal.
